# Fritzing sketch RPM_Layout (saved by Fritzing 1.0.5)
circuit board: 8.46667cm x 5.64444cm
breadboards: 1

parts:
  U1 = ESP32S-HiLetgo [part_number=ESP32S-HiLetgo]
  U2 = SBX DSUN [package=THT]
  U3 = TLP621 [package=THT]
  R1 = Resistor [tolerance=±5% resistance=2.2k package="0603 [SMD]"]
  JP1 = Header 3 [package=jst-3-pth]
  RGB_SMD_LED1 = SMD RGB LED (WS2812) [package=5050]
  C1 = Capacitor Polarized [package=cpol-radial-100uf-25v]

nets:
  N1: U1.3.3, U3.Pin_4
  N2: U1.GPIO12, RGB_SMD_LED1.DIn
  GND: U1.GND, U2.GND, R1.Pin_1, JP1.1, RGB_SMD_LED1.VSS, C1.-
  N3: U1.GPIO10, U3.Pin_3
  VIN: U1.VIN, U2.+VOUT, RGB_SMD_LED1.VDD, C1.+
  N4: U2.+VIN, JP1.3
  N5: U3.Pin_1, JP1.2
  N6: U3.Pin_2, R1.Pin_0

notes:
  Connector to Motorcycle
  12v +
  12V -
  12 V RPM Signal
  Optocoupler
  12V to 5v DC-DC Converter
  LED Strip with x Leds
  Cap because i had issues with ESP32 Wifi drawing to much current

custom parts:
  ESP32S-HiLetgo: HiLetgo ESP-WROOM-32 ESP32 ESP-32S Development Board 2.4GHz Dual-Mode WiFi + Bluetooth Dual Cores Microcontroller The ESP32 integrated with Antenna switches, RF Balun, power amplifiers, low-noise amplifiers, filters, and management modules, and the entire solution occupies the least area of PCB. 2.4 GHz Wi-Fi plus Bluetooth dual-mode chip, with TSMC Ultra-low power consumption 40nm technology,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
  SBX DSUN: SBX DSUN input voltage 4.5 - 28V DC output voltage .8v to 20VDC (step down converter) Output current 3A max
